# Fritzing sketch 1 (saved by Fritzing 0.9.3b)
circuit board: 16.9333cm x 5.64444cm
breadboards: 1

parts:
  元件1 = Arduino Nano (Rev3.0)
  Nokia_5110_LCD_Module1 = Nokia5110LCDModule
  M1 = DC Motor
  S1 = H-Bridge with L298N
  KY-1 = Keyes Relay [package=THT]
  D2 = Rectifier Diode 500mil [part_number=1N4001 package="500 mil [THT]"]
  进水电磁阀 = Peltier Element
  排水电磁阀 = Peltier Element
  KY-2 = Keyes Relay [package=THT]
  Power_plug1 = Power plug
  D1 = Rectifier Diode 500mil [part_number=1N4001 package="500 mil [THT]"]
  U1 = TTP223 [package=sot23-6]
  U2 = TTP223 [package=sot23-6]
  U3 = TTP223 [package=sot23-6]

nets:
  GND: 元件1.GND, Nokia_5110_LCD_Module1.Grnd, S1.GND, KY-1.ground, KY-2.ground, Power_plug1.GND, U1.GND, U2.GND, U3.GND
  N1: 元件1.D2, U3.I/O
  N2: 元件1.D3, Nokia_5110_LCD_Module1.SCLK
  N3: 元件1.D4, Nokia_5110_LCD_Module1.6_DN_(MOSI)
  N4: 元件1.D5, Nokia_5110_LCD_Module1.D/C
  N5: 元件1.D6, Nokia_5110_LCD_Module1.SCE
  N6: 元件1.D7, Nokia_5110_LCD_Module1.RST
  VCC: 元件1.VIN, Nokia_5110_LCD_Module1.Vcc, S1.5V, KY-1.power, KY-2.power, U1.VCC, U2.VCC, U3.VCC
  N7: 元件1.A5, U1.I/O
  N8: 元件1.A4, KY-2.signal
  N9: 元件1.A3, KY-1.signal
  N10: 元件1.A2, S1.IN2
  N11: 元件1.A1, S1.IN1
  N12: 元件1.A0, U2.I/O
  N13: 元件1.3V3, Nokia_5110_LCD_Module1.LED
  N14: M1.pin_1, M1.pin_2, S1.M2-01, S1.M2-02, S1.ENA-5V
  12V: S1.12V, KY-1.C, KY-2.C, Power_plug1.VCC
  N15: KY-1.NO, D2.cathode, 排水电磁阀.pin2
  N16: D2.anode, 进水电磁阀.pin1, 排水电磁阀.pin1, D1.anode
  N17: 进水电磁阀.pin2, KY-2.NO, D1.cathode

notes:
  T(Start)
  T(Time)
  L(Stop)
  进继
  排继

custom parts:
  : Nokia 5110 LCD with 8 pin. It's a 45mm*45mm module part. Description: The Nokia 5110 is a basic graphic LCD screen for lots of applications. It was originally intended for as a cell phone screen. This one is mounted on an easy to solder PCB. It uses the PCD8544 controller. The PCD8544 is a low power CMOS LCD controller/driver, designed to drive a graphic display of 48 rows and 84 columns. All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
  H-Bridge with L298N: h-bridge
  Keyes Relay: The Keyes 5V relay module is suitable for SCM development, home appliance control. It uses a 5V~12V TIL control signal which can control DC / AC signal.
  Rectifier Diode 500mil: A standard rectifier diode streched to 500mil
  TTP223: Touch Sensor
